// Logisim project DDCA 2.circ as structural Verilog: 1 circuit, main circuit main
module main (
  input  Slot1,
  input  Slot2,
  input  Slot3,
  input  sloat4,
  output Entry_Gate
);

  wire AND_Gate_out;

  LED Available (.in(Entry_Gate));
  and AND_Gate (AND_Gate_out, Slot1, Slot2, sloat4, sloat4);
  not NOT_Gate (Entry_Gate, AND_Gate_out);
  LED FULL (.in(AND_Gate_out));

  assign Slot3 = sloat4;
endmodule
